# Fritzing sketch Communication NodeMCU and Arduino_Schematic Diagram (saved by Fritzing 0.9.10b)

parts:
  U1 = NodeMCU V1.0
  Part1 = Arduino Uno (Rev3)
  R1 = Resistor [tolerance=±5% power=0.25 resistance=220 package=THT]
  LED1 = LED - 3mm [color="Red (633nm)" current=0.030 package="3 mm [THT]"]

nets:
  N1: U1.D1, Part1.A4/SDA
  N2: U1.D2, Part1.A5/SCL
  GND: U1.GND, Part1.GND, LED1.cathode
  N3: Part1.D5_PWM, R1.Pin_0
  N4: R1.Pin_1, LED1.anode

custom parts:
  NodeMCU V1.0: ESP8266 based NodeMCU
